# Fritzing sketch Garage (saved by Fritzing 0.9.3b)

parts:
  U1 = NodeMCU V1.0
  U2 = 2-Channel 5v Relay Shield [package=relay-2ch5v10a]
  U3 = mystery part, 3 pins [chip_label=?]
  U4 = mystery part, 3 pins [chip_label=?]
  S1 = Reed switch [package=THT]
  S4 = Reed switch [package=THT]

nets:
  N1: U1.D0, U2.IN1
  N2: U1.D1, U2.IN2
  N3: U1.D2, S1.pin_2
  N4: U1.D3, S4.pin_2
  GND: U1.GND, U2.GND, S1.pin_1, S4.pin_1
  VIN: U1.Vin, U2.VCC
  N5: U2.K1-In, U4.pin1
  N6: U2.K1-On, U4.pin3
  N7: U2.K2-In, U3.pin1
  N8: U2.K2-On, U3.pin2, U3.pin3

notes:
  Garage
  Door 1
  Garage
  Door 2
  USB Power

custom parts:
  NodeMCU V1.0: ESP9266 based NodeMCU
  2-Channel 5v Relay Shield: 2 Channel 5v Relay Shield w. 2x SPD-06VDC-SD-C
